# Fritzing sketch DeskBuddyController (saved by Fritzing 0.9.3b)
circuit board: 15.6342cm x 12.8214cm
stripboards: 1

parts:
  U1 = NodeMCU V1.0
  DHT1 = DHT22 Humidity and Temperature Sensor
  U4 = Logic Level Converter
  R1 = Resistor [tolerance=±5% resistance=2.2k package=THT]
  R2 = Resistor [tolerance=±5% resistance=2.2k package=THT]
  R4 = Resistor [tolerance=±5% resistance=2.2k package=THT]
  R3 = Resistor [tolerance=±5% resistance=2.2k package=THT]
  J4 = male pin header, 4 pins [form="♂ (male)"]

nets:
  N1: U1.D2, DHT1.DATA
  N2: U1.D4, U4.TX_LV, R1.Pin_1
  3.3V: U1.3V3, U4.LV, R1.Pin_0, R2.Pin_1
  GND: U1.GND, DHT1.GND, U4.GND, J4.pin4
  N3: U1.D5, U4.TX2_LV, R2.Pin_0
  5V: U1.Vin, DHT1.VDD, U4.HV, R4.Pin_1, R3.Pin_0, J4.pin3
  N4: U4.TX_HV, R3.Pin_1, J4.pin2
  N5: U4.TX2_HV, R4.Pin_0, J4.pin1

notes:
  SDA
  SCL

custom parts:
  NodeMCU V1.0: ESP9266 based NodeMCU
